# Fritzing sketch Espressiot_final_Oled (saved by Fritzing 0.9.3b)
stripboards: 2

parts:
  Part1 = Adafruit MAX31865 RTD Sensor Breakout [part_number="Adafruit #3328"]
  U1 = ESP-12F (ESP8266 WiFi Module) [part_number=ESP8266]
  R2 = Resistor [tolerance=±5% resistance=4.7k package=THT]
  R3 = Resistor [tolerance=±5% resistance=1k package=THT]
  R4 = Resistor [tolerance=±5% resistance=10k package=THT]
  S1 = Taiway 100-SP-X-T1 SPDT Miniature Toggle Switch [part_number="Steam Switch" package=THT]
  J1 = female pin header, 1 pin [form="♀ (female)" part_number="SSR -"]
  R1 = Resistor [tolerance=±5% resistance=1k part_number="RTD Pt 4 wires" package=THT]
  J2 = female pin header, 1 pin [form="♀ (female)"]
  J2_2 = female pin header, 1 pin [form="♀ (female)" part_number="SSR +"]  # not connected
  J4 = female pin header, 1 pin [form="♀ (female)" part_number="- "]
  J6 = female pin header, 1 pin [form="♀ (female)" part_number="AC in"]  # not connected
  J5 = female pin header, 1 pin [form="♀ (female)" part_number="AC in"]  # not connected
  J3 = female pin header, 1 pin [form="♀ (female)" part_number="+ 3.3 volts"]
  J7 = male pin header, 2 pins [form="♂ (male)"]
  J8 = male pin header, 1 pin [form="♂ (male)"]
  Mod1 = OLED Mono 0.56 inch blue or white
  U2 = ESP-12F (ESP8266 WiFi Module) [part_number=ESP8266]
  R5 = Resistor [tolerance=±5% resistance=4.7k package=THT]
  J10 = female alternating pin header, 1 pin [form="♀ (female)"]
  J12 = female alternating pin header, 1 pin [form="♀ (female)"]
  J13 = female alternating pin header, 1 pin [form="♀ (female)"]
  J14 = female alternating pin header, 1 pin [form="♀ (female)"]
  J9 = female alternating pin header, 1 pin [form="♀ (female)"]
  J15 = female pin header, 1 pin [form="♀ (female)" part_number="AC in"]  # not connected
  J16 = female pin header, 1 pin [form="♀ (female)" part_number="AC in"]  # not connected

nets:
  VIN: Part1.VIN, U1.VCC, U1.EN, S1.L2, J3.pin1
  GND: Part1.GND, U1.GND, R2.Pin_1, R4.Pin_1, J1.pin1, J4.pin1, J8.pin1
  N1: Part1.SCLK, U1.GPIO13
  N2: Part1.SDO, U1.GPIO12
  N3: Part1.SDI, U1.GPIO14
  N4: Part1.CS, U1.GPIO16
  N5: Part1.RTDIN+, Part1.FORCE+, R1.Pin_1
  N6: Part1.FORCE-, Part1.RTDIN-, R1.Pin_0
  N7: U1.RXD0, J7.pin2
  N8: U1.TXD0, J7.pin1
  N9: U1.GPIO15, R2.Pin_0
  N10: U1.GPIO4, R3.Pin_0
  N11: U1.GPIO5, J2.pin1
  N12: R3.Pin_1, R4.Pin_0, S1.COM
  N13: Mod1.SDA, U2.GPIO4
  N14: Mod1.SCL, U2.GPIO5
  VCC: Mod1.VCC, U2.VCC, U2.EN, J9.pin1
  GND_2: Mod1.GND, U2.GND, R5.Pin_1, J10.pin1, J14.pin1
  N15: U2.RXD0, J13.pin1
  N16: U2.TXD0, J12.pin1
  N17: U2.GPIO15, R5.Pin_0

notes:
  Steam switch
  SSR
  120 Vac
  3.3 Vdc
  +
  -
  TXD
  RXD
  GND
  + rail
  - rail
  https://www.aliexpress.com/item/32396963332.html?spm=a2g0s.9042311.0.0.27424c4dCR7MIh
  Portable ESP8266 display module
  My code is for a 128x32 oled display, SSD1306
  https://www.google.com/search?q=0.91+oled+i2c
  120 vac

custom parts:
  Adafruit MAX31865 RTD Sensor Breakout: For precision temperature sensing, nothing beats a Platinum RTD. Resistance temperature detectors (RTDs) are temperature sensors that contain a resistor that changes resistance value as its temperature changes, basically a kind of thermistor. In this sensor, the resistor is actually a small strip of Platinum with a resistance of 100 ohms at 0°C, thus the name PT100. Compared to most NTC/PTC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
  ESP-12F (ESP8266 WiFi Module): WiFi Module based on the ESP8266 with onboard PCB antenna and UART communications
  OLED Mono 0.56 inch blue or white: OLED, I2C 3.3V - 5V Blue and White text versions
